// Logisim project control-logic.circ as structural Verilog: 1 circuit, main circuit control_logic
module control_logic (
  input  [31:0] Instruction,
  input  BrEq,
  input  BrLt,
  output PCSel,
  output RegWEn,
  output [2:0] ImmSel,
  output BrUn,
  output ASel,
  output BSel,
  output [3:0] ALUSel,
  output MemWEn,
  output [1:0] WBSel
);

  wire add, addi, and_14_out, and_15_out, and_16_out, and_17_out, and_or_sub_or_mul, andi, auipc, beq, bge,
       bgeu, blt, bltu, bne, comparator_1_eq, comparator_2_eq, comparator_3_eq, comparator_4_eq,
       comparator_5_eq, comparator_6_eq, comparator_7_eq, comparator_8_eq, comparator_9_eq, comparator_10_eq,
       comparator_11_eq, comparator_12_eq, comparator_13_eq, comparator_14_eq, comparator_15_eq,
       comparator_16_eq, comparator_17_eq, comparator_18_eq, comparator_19_eq, comparator_20_eq,
       comparator_21_eq, comparator_22_eq, comparator_23_eq, comparator_24_eq, comparator_25_eq,
       comparator_26_eq, comparator_27_eq, comparator_28_eq, comparator_29_eq, comparator_30_eq,
       comparator_31_eq, comparator_32_eq, comparator_33_eq, comparator_34_eq, comparator_35_eq,
       comparator_40_eq, comparator_41_eq, comparator_42_eq, comparator_43_eq, comparator_44_eq,
       comparator_45_eq, comparator_46_eq, is_and, is_mulhul, is_or, is_sll, is_slt, is_sra, is_srl, is_xor,
       Jal, Jalr, lb, lh, lui, lw, mul, mulh, not_1_out, not_2_out, or_2_out, or_3_out, or_4_out, ori, sb,
       sh, sll_or_mulh, slli, slli_func3, slti, sr_func3, srai, srl_or_sra, srli, sub, sw, xori;
  wire [5:0] ROMInput;
  wire [15:14] rom_1_data;

  Comparator #(.width(7)) comparator_1 (.a(Instruction[31:25]), .b(7'b0100000), .eq(comparator_1_eq));  // open: gt, lt
  Comparator #(.width(7)) comparator_2 (.a(Instruction[31:25]), .b({7{1'b0}}), .eq(comparator_2_eq));  // open: gt, lt
  Comparator #(.width(7)) comparator_3 (.a(Instruction[31:25]), .b({7{1'b0}}), .eq(comparator_3_eq));  // open: gt, lt
  and and_1 (srai, comparator_1_eq, sr_func3);
  and and_2 (srli, comparator_2_eq, sr_func3);
  and and_3 (slli, comparator_3_eq, slli_func3);
  ROM #(.addrWidth(6), .dataWidth(16)) rom_1 (
    .addr(ROMInput), .data({rom_1_data, WBSel, MemWEn, ALUSel, BSel, ASel, BrUn, ImmSel, RegWEn}));
  Comparator #(.width(3)) comparator_4 (.a(Instruction[14:12]), .b(3'b000), .eq(comparator_4_eq));  // open: gt, lt
  Comparator #(.width(3)) comparator_5 (.a(Instruction[14:12]), .b(3'b001), .eq(comparator_5_eq));  // open: gt, lt
  Comparator #(.width(3)) comparator_6 (.a(Instruction[14:12]), .b(3'b010), .eq(comparator_6_eq));  // open: gt, lt
  Comparator #(.width(3)) comparator_7 (.a(Instruction[14:12]), .b(3'b100), .eq(comparator_7_eq));  // open: gt, lt
  Comparator #(.width(3)) comparator_8 (.a(Instruction[14:12]), .b(3'b101), .eq(comparator_8_eq));  // open: gt, lt
  Comparator #(.width(3)) comparator_9 (.a(Instruction[14:12]), .b(3'b110), .eq(comparator_9_eq));  // open: gt, lt
  Comparator #(.width(3)) comparator_10 (.a(Instruction[14:12]), .b(3'b111), .eq(comparator_10_eq));  // open: gt, lt
  Comparator #(.width(7)) comparator_11 (.a(Instruction[6:0]), .b(7'b0010011), .eq(comparator_11_eq));  // open: gt, lt
  and and_4 (addi, comparator_4_eq, comparator_11_eq);
  and and_5 (slli_func3, comparator_5_eq, comparator_11_eq);
  and and_6 (slti, comparator_6_eq, comparator_11_eq);
  and and_7 (xori, comparator_7_eq, comparator_11_eq);
  and and_8 (sr_func3, comparator_8_eq, comparator_11_eq);
  and and_9 (ori, comparator_9_eq, comparator_11_eq);
  and and_10 (andi, comparator_10_eq, comparator_11_eq);
  Comparator #(.width(7)) comparator_12 (.a(Instruction[6:0]), .b(7'b0000011), .eq(comparator_12_eq));  // open: gt, lt
  Comparator #(.width(3)) comparator_13 (.a(Instruction[14:12]), .b(3'b000), .eq(comparator_13_eq));  // open: gt, lt
  Comparator #(.width(3)) comparator_14 (.a(Instruction[14:12]), .b(3'b001), .eq(comparator_14_eq));  // open: gt, lt
  Comparator #(.width(3)) comparator_15 (.a(Instruction[14:12]), .b(3'b010), .eq(comparator_15_eq));  // open: gt, lt
  and and_11 (lb, comparator_13_eq, comparator_12_eq);
  and and_12 (lh, comparator_14_eq, comparator_12_eq);
  and and_13 (lw, comparator_15_eq, comparator_12_eq);
  or or_1 (PCSel, Jal, or_2_out, Jalr);
  or or_2 (or_2_out, and_14_out, and_15_out, and_16_out, and_17_out);
  and and_14 (and_14_out, BrEq, beq);
  not not_1 (not_1_out, BrEq);
  and and_15 (and_15_out, not_1_out, bne);
  and and_16 (and_16_out, BrLt, or_3_out);
  not not_2 (not_2_out, BrLt);
  and and_17 (and_17_out, not_2_out, or_4_out);
  Comparator #(.width(3)) comparator_16 (.a(Instruction[14:12]), .b(3'b000), .eq(comparator_16_eq));  // open: gt, lt
  Comparator #(.width(3)) comparator_17 (.a(Instruction[14:12]), .b(3'b001), .eq(comparator_17_eq));  // open: gt, lt
  Comparator #(.width(3)) comparator_18 (.a(Instruction[14:12]), .b(3'b010), .eq(comparator_18_eq));  // open: gt, lt
  Comparator #(.width(7)) comparator_19 (.a(Instruction[6:0]), .b(7'b1100011), .eq(comparator_19_eq));  // open: gt, lt
  Comparator #(.width(3)) comparator_20 (.a(Instruction[14:12]), .b(3'b000), .eq(comparator_20_eq));  // open: gt, lt
  Comparator #(.width(3)) comparator_21 (.a(Instruction[14:12]), .b(3'b101), .eq(comparator_21_eq));  // open: gt, lt
  Comparator #(.width(3)) comparator_22 (.a(Instruction[14:12]), .b(3'b111), .eq(comparator_22_eq));  // open: gt, lt
  Comparator #(.width(3)) comparator_23 (.a(Instruction[14:12]), .b(3'b100), .eq(comparator_23_eq));  // open: gt, lt
  Comparator #(.width(3)) comparator_24 (.a(Instruction[14:12]), .b(3'b110), .eq(comparator_24_eq));  // open: gt, lt
  Comparator #(.width(3)) comparator_25 (.a(Instruction[14:12]), .b(3'b001), .eq(comparator_25_eq));  // open: gt, lt
  Comparator #(.width(7)) comparator_26 (.a(Instruction[6:0]), .b(7'b0100011), .eq(comparator_26_eq));  // open: gt, lt
  and and_18 (sb, comparator_16_eq, comparator_26_eq);
  and and_19 (sh, comparator_17_eq, comparator_26_eq);
  and and_20 (sw, comparator_18_eq, comparator_26_eq);
  or or_3 (or_3_out, blt, bltu);
  or or_4 (or_4_out, bge, bgeu);
  and and_21 (beq, comparator_20_eq, comparator_19_eq);
  and and_22 (bge, comparator_21_eq, comparator_19_eq);
  and and_23 (bgeu, comparator_22_eq, comparator_19_eq);
  and and_24 (blt, comparator_23_eq, comparator_19_eq);
  and and_25 (bltu, comparator_24_eq, comparator_19_eq);
  and and_26 (bne, comparator_25_eq, comparator_19_eq);
  // Priority_Encoder #(.select_enc(6)) priority_encoder_1: pin names not known; wires that end beside it: ROMInput, add, mul, sub, is_sll, mulh, is_mulhul, is_slt, is_xor, is_srl, is_sra, is_or, is_and, lb, lh, lw, addi, slli, slti, xori, srli, srai, ori, andi, sb, sh, sw, beq, bne, blt, bge, bltu, bgeu, auipc, lui, Jal, Jalr
  Comparator #(.width(7)) comparator_27 (.a(Instruction[6:0]), .b(7'b0110011), .eq(comparator_27_eq));  // open: gt, lt
  Comparator #(.width(3)) comparator_28 (.a(Instruction[14:12]), .b(3'b000), .eq(comparator_28_eq));  // open: gt, lt
  Comparator #(.width(3)) comparator_29 (.a(Instruction[14:12]), .b(3'b111), .eq(comparator_29_eq));  // open: gt, lt
  Comparator #(.width(3)) comparator_30 (.a(Instruction[14:12]), .b(3'b110), .eq(comparator_30_eq));  // open: gt, lt
  Comparator #(.width(3)) comparator_31 (.a(Instruction[14:12]), .b(3'b100), .eq(comparator_31_eq));  // open: gt, lt
  Comparator #(.width(3)) comparator_32 (.a(Instruction[14:12]), .b(3'b001), .eq(comparator_32_eq));  // open: gt, lt
  Comparator #(.width(3)) comparator_33 (.a(Instruction[14:12]), .b(3'b101), .eq(comparator_33_eq));  // open: gt, lt
  Comparator #(.width(3)) comparator_34 (.a(Instruction[14:12]), .b(3'b010), .eq(comparator_34_eq));  // open: gt, lt
  Comparator #(.width(3)) comparator_35 (.a(Instruction[14:12]), .b(3'b011), .eq(comparator_35_eq));  // open: gt, lt
  Comparator #(.width(7)) comparator_36 (.a(Instruction[6:0]), .b(7'b1101111), .eq(Jal));  // open: gt, lt
  Comparator #(.width(7)) comparator_37 (.a(Instruction[6:0]), .b(7'b1100111), .eq(Jalr));  // open: gt, lt
  Comparator #(.width(7)) comparator_38 (.a(Instruction[6:0]), .b(7'b0010111), .eq(auipc));  // open: gt, lt
  Comparator #(.width(7)) comparator_39 (.a(Instruction[6:0]), .b(7'b0110111), .eq(lui));  // open: gt, lt
  and and_27 (and_or_sub_or_mul, comparator_28_eq, comparator_27_eq);
  and and_28 (is_and, comparator_29_eq, comparator_27_eq);
  and and_29 (is_or, comparator_30_eq, comparator_27_eq);
  and and_30 (is_xor, comparator_31_eq, comparator_27_eq);
  and and_31 (sll_or_mulh, comparator_32_eq, comparator_27_eq);
  and and_32 (srl_or_sra, comparator_33_eq, comparator_27_eq);
  and and_33 (is_slt, comparator_34_eq, comparator_27_eq);
  and and_34 (is_mulhul, comparator_35_eq, comparator_27_eq);
  Comparator #(.width(7)) comparator_40 (.a(Instruction[31:25]), .b({7{1'b0}}), .eq(comparator_40_eq));  // open: gt, lt
  Comparator #(.width(7)) comparator_41 (
    .a(Instruction[31:25]), .b(7'b0100000), .eq(comparator_41_eq));  // open: gt, lt
  Comparator #(.width(7)) comparator_42 (
    .a(Instruction[31:25]), .b(7'b0000001), .eq(comparator_42_eq));  // open: gt, lt
  Comparator #(.width(7)) comparator_43 (.a(Instruction[31:25]), .b({7{1'b0}}), .eq(comparator_43_eq));  // open: gt, lt
  Comparator #(.width(7)) comparator_44 (
    .a(Instruction[31:25]), .b(7'b0000001), .eq(comparator_44_eq));  // open: gt, lt
  Comparator #(.width(7)) comparator_45 (.a(Instruction[31:25]), .b({7{1'b0}}), .eq(comparator_45_eq));  // open: gt, lt
  Comparator #(.width(7)) comparator_46 (
    .a(Instruction[31:25]), .b(7'b0100000), .eq(comparator_46_eq));  // open: gt, lt
  and and_35 (add, comparator_40_eq, and_or_sub_or_mul);
  and and_36 (sub, comparator_41_eq, and_or_sub_or_mul);
  and and_37 (mul, comparator_42_eq, and_or_sub_or_mul);
  and and_38 (is_sll, comparator_43_eq, sll_or_mulh);
  and and_39 (mulh, comparator_44_eq, sll_or_mulh);
  and and_40 (is_srl, comparator_45_eq, srl_or_sra);
  and and_41 (is_sra, comparator_46_eq, srl_or_sra);

  // Other names for the same wires on the sheet: func7[6:0] = Instruction[31:25]

  // Notes on the sheet:
  //   I-TYPE
  //   Load
  //   INPUTS to your circuit
  //   Connect ROM Input here ->
  //   Opcode
  //   func3
  //   func7
  //   Opcode
  //   func7
  //   contents of rom_1 (hex, n*v repeats v):
  //   1001 1401 1601 1081 1481 1581 1101 1201 1281 1681 1301 1381 41 41 41 1041 10c1 1141 1241 12c1 16c1
  //   1341 13c1 842 842 842 4*64 74 74 1067 17c7 2069 2041
  //   func3
  //   ROM FOR CONTROL LOGIC
  //   DON'T CHANGE THE LOCATIONS OF THE INPUTS AND OUTPUTS!
  //   This is only if you choose to do the ROM option
  //   CONNECT
  //   WIRE
  //   TO
  //   USE
  //   ROM
  //   OUTPUT from your circuit
  //   B-TYPE
  //   Store
  //   func7
  //   Reminder: If using ROM, use combinational logic for PCSel
  //   Opcode
  //   func7
  //   Opcode
  //   func3
  //   func3
  //   R-TYPE
  //   OTHER
  //   func7
  //   Opcode
  //   func3
endmodule
