// Logisim project partial-load.circ as structural Verilog: 1 circuit, main circuit partial_load
module partial_load (
  input  [31:0] Instruction,
  input  [31:0] MemAddress,
  input  [31:0] DataFromMem,
  output [31:0] DataToReg
);

  wire and_4_out, and_5_out, and_6_out, and_7_out, and_8_out, and_9_out, and_10_out, comparator_8_eq,
       comparator_9_eq, comparator_10_eq, comparator_11_eq, lb, lh, load_half, load_word, loadbyte, lw, Mem0,
       Mem1, Mem2, Mem3;
  wire [2:0] MemLoc;
  wire [31:0] MemAd0, MemAd01, MemAd1, MemAd2, MemAd3, MemAd12, MemAd23;

  Comparator #(.width(2)) comparator_1 (.a(2'b00), .b(MemAddress[1:0]), .eq(Mem0));  // open: gt, lt
  Comparator #(.width(2)) comparator_2 (.a(2'b01), .b(MemAddress[1:0]), .eq(Mem1));  // open: gt, lt
  Comparator #(.width(2)) comparator_3 (.a(2'b10), .b(MemAddress[1:0]), .eq(Mem2));  // open: gt, lt
  Comparator #(.width(2)) comparator_4 (.a(2'b11), .b(MemAddress[1:0]), .eq(Mem3));  // open: gt, lt
  Comparator #(.width(3)) comparator_5 (.a(3'b000), .b(Instruction[14:12]), .eq(loadbyte));  // open: gt, lt
  Comparator #(.width(3)) comparator_6 (.a(3'b001), .b(Instruction[14:12]), .eq(load_half));  // open: gt, lt
  Comparator #(.width(3)) comparator_7 (.a(3'b010), .b(Instruction[14:12]), .eq(load_word));  // open: gt, lt
  Comparator #(.width(7)) comparator_8 (.a(Instruction[6:0]), .b(7'b0000011), .eq(comparator_8_eq));  // open: gt, lt
  Comparator #(.width(3)) comparator_9 (.a(Instruction[14:12]), .b(3'b000), .eq(comparator_9_eq));  // open: gt, lt
  Comparator #(.width(3)) comparator_10 (.a(Instruction[14:12]), .b(3'b001), .eq(comparator_10_eq));  // open: gt, lt
  Comparator #(.width(3)) comparator_11 (.a(Instruction[14:12]), .b(3'b010), .eq(comparator_11_eq));  // open: gt, lt
  and and_1 (lb, comparator_9_eq, comparator_8_eq);
  and and_2 (lh, comparator_10_eq, comparator_8_eq);
  and and_3 (lw, comparator_11_eq, comparator_8_eq);
  and and_4 (and_4_out, Mem0, loadbyte);
  and and_5 (and_5_out, Mem1, loadbyte);
  and and_6 (and_6_out, Mem2, loadbyte);
  and and_7 (and_7_out, Mem3, loadbyte);
  and and_8 (and_8_out, Mem0, load_half);
  and and_9 (and_9_out, Mem1, load_half);
  and and_10 (and_10_out, Mem2, load_half);
  Priority_Encoder priority_encoder_1 (
    .in0(and_4_out), .in1(and_5_out), .in2(and_6_out), .in3(and_7_out), .in4(and_8_out), .in5(and_9_out),
    .in6(and_10_out), .in7(load_word), .out(MemLoc));  // open: en_in, gs, en_out
  assign MemAd0 = {{24{DataFromMem[7]}}, DataFromMem[7:0]};  // Bit_Extender bit_extender_1
  assign MemAd1 = {{24{DataFromMem[15]}}, DataFromMem[15:8]};  // Bit_Extender bit_extender_2
  assign MemAd2 = {{24{DataFromMem[23]}}, DataFromMem[23:16]};  // Bit_Extender bit_extender_3
  assign MemAd3 = {{24{DataFromMem[31]}}, DataFromMem[31:24]};  // Bit_Extender bit_extender_4
  assign MemAd01 = {{16{DataFromMem[15]}}, DataFromMem[15:0]};  // Bit_Extender bit_extender_5
  assign MemAd12 = {{16{DataFromMem[23]}}, DataFromMem[23:8]};  // Bit_Extender bit_extender_6
  assign MemAd23 = {{16{DataFromMem[31]}}, DataFromMem[31:16]};  // Bit_Extender bit_extender_7
  Multiplexer #(.select(3), .width(32)) multiplexer_1 (
    .in0(MemAd0), .in1(MemAd1), .in2(MemAd2), .in3(MemAd3), .in4(MemAd01), .in5(MemAd12), .in6(MemAd23),
    .in7(DataFromMem), .out(DataToReg), .sel(MemLoc));

  // Notes on the sheet:
  //   INPUTS to your circuit
  //   Opcode
  //   func7
  //   func3
  //   DON'T CHANGE THE LOCATIONS OF THE INPUTS AND OUTPUTS!
  //   OUTPUT from your circuit
endmodule
