// Logisim project partial-store.circ as structural Verilog: 1 circuit, main circuit partial_store
module partial_store (
  input  [31:0] Instruction,
  input  [31:0] MemAddress,
  input  [31:0] DataFromReg,
  input  MemWEn,
  output [3:0] MemWriteMask,
  output [31:0] DataToMem
);

  wire and_4_out, and_5_out, and_6_out, and_7_out, and_8_out, and_9_out, comparator_1_eq, comparator_2_eq,
       comparator_3_eq, comparator_4_eq, MemAd0, MemAd1, MemAd2, MemAd3, not_1_out, sb, sh, sw;

  Comparator #(.width(7)) comparator_1 (.a(Instruction[6:0]), .b(7'b0100011), .eq(comparator_1_eq));  // open: gt, lt
  Comparator #(.width(3)) comparator_2 (.a(Instruction[14:12]), .b(3'b000), .eq(comparator_2_eq));  // open: gt, lt
  Comparator #(.width(3)) comparator_3 (.a(Instruction[14:12]), .b(3'b001), .eq(comparator_3_eq));  // open: gt, lt
  Comparator #(.width(3)) comparator_4 (.a(Instruction[14:12]), .b(3'b010), .eq(comparator_4_eq));  // open: gt, lt
  Comparator #(.width(2)) comparator_5 (.a(MemAddress[1:0]), .b(2'b00), .eq(MemAd0));  // open: gt, lt
  Comparator #(.width(2)) comparator_6 (.a(MemAddress[1:0]), .b(2'b01), .eq(MemAd1));  // open: gt, lt
  Comparator #(.width(2)) comparator_7 (.a(MemAddress[1:0]), .b(2'b10), .eq(MemAd2));  // open: gt, lt
  Comparator #(.width(2)) comparator_8 (.a(MemAddress[1:0]), .b(2'b11), .eq(MemAd3));  // open: gt, lt
  and and_1 (sb, comparator_1_eq, comparator_2_eq);
  and and_2 (sh, comparator_1_eq, comparator_3_eq);
  and and_3 (sw, comparator_1_eq, comparator_4_eq);
  and and_4 (and_4_out, sb, MemAd0);
  and and_5 (and_5_out, sb, MemAd1);
  and and_6 (and_6_out, sb, MemAd2);
  and and_7 (and_7_out, sb, MemAd3);
  and and_8 (and_8_out, sh, MemAd0);
  and and_9 (and_9_out, sh, MemAd2);
  not not_1 (not_1_out, MemWEn);
  Multiplexer #(.select(4), .width(32)) multiplexer_1 (
    .in0({32{1'b0}}), .in1({{24{1'b0}}, DataFromReg[7:0]}), .in2({{16{1'b0}}, DataFromReg[7:0], {8{1'b0}}}),
    .in3({{16{1'b0}}, DataFromReg[15:0]}), .in4({{8{1'b0}}, DataFromReg[7:0], {16{1'b0}}}), .in5({32{1'b0}}),
    .in6({32{1'b0}}), .in7({32{1'b0}}), .in8({DataFromReg[7:0], {24{1'b0}}}), .in9({32{1'b0}}),
    .in10({32{1'b0}}), .in11({32{1'b0}}), .in12({DataFromReg[15:0], {16{1'b0}}}), .in13({32{1'b0}}),
    .in14({32{1'b0}}), .in15(DataFromReg), .out(DataToMem), .sel(MemWriteMask));
  Priority_Encoder #(.select_enc(4)) priority_encoder_1 (
    .in0(not_1_out), .in1(and_4_out), .in2(and_5_out), .in3(and_8_out), .in4(and_6_out), .in8(and_7_out),
    .in12(and_9_out), .in15(sw), .out(MemWriteMask));  // open: in5, in6, in7, in9, in10, in11, in13, in14, gs, en_out, en_in

  // Other names for the same wires on the sheet: DataFromReg8Bits[7:0] = DataFromReg[7:0]

  // Notes on the sheet:
  //   INPUTS to your circuit
  //   DON'T CHANGE THE LOCATIONS OF THE INPUTS AND OUTPUTS!
  //   OUTPUT from your circuit
endmodule
