// Logisim project regfile.circ as structural Verilog: 1 circuit, main circuit regfile
module regfile (
  input  [4:0] ReadIndex1,
  input  [4:0] ReadIndex2,
  input  [4:0] WriteIndex,
  input  [31:0] WriteData,
  input  RegWEn,
  input  clk,
  output [31:0] ra,
  output [31:0] sp,
  output [31:0] t0,
  output [31:0] t1,
  output [31:0] t2,
  output [31:0] s0,
  output [31:0] s1,
  output [31:0] a0,
  output [31:0] ReadData1,
  output [31:0] ReadData2
);

  wire WEN0, WEN1, WEN2, WEN3, WEN4, WEN5, WEN6, WEN7, WEN8, WEN9, WEN10, WEN11, WEN12, WEN13, WEN14, WEN15,
       WEN16, WEN17, WEN18, WEN19, WEN20, WEN21, WEN22, WEN23, WEN24, WEN25, WEN26, WEN27, WEN28, WEN29,
       WEN30, WEN31;
  wire [31:0] x3, x4, x11, x12, x13, x14, x15, x16, x17, x18, x19, x20, x21, x22, x23, x24, x25, x26, x27,
       x28, x29, x30, x31;

  Demultiplexer #(.select(5)) demultiplexer_1 (
    .out0(WEN0), .out1(WEN1), .out2(WEN2), .out3(WEN3), .out4(WEN4), .out5(WEN5), .out6(WEN6), .out7(WEN7),
    .out8(WEN8), .out9(WEN9), .out10(WEN10), .out11(WEN11), .out12(WEN12), .out13(WEN13), .out14(WEN14),
    .out15(WEN15), .out16(WEN16), .out17(WEN17), .out18(WEN18), .out19(WEN19), .out20(WEN20), .out21(WEN21),
    .out22(WEN22), .out23(WEN23), .out24(WEN24), .out25(WEN25), .out26(WEN26), .out27(WEN27), .out28(WEN28),
    .out29(WEN29), .out30(WEN30), .out31(WEN31), .in(RegWEn), .sel(WriteIndex));
  Register #(.width(32)) register_1 (.D(WriteData), .en(WEN1), .clk(clk), .Q(ra));  // open: clr
  Register #(.width(32)) register_2 (.D(WriteData), .en(WEN2), .clk(clk), .Q(sp));  // open: clr
  Register #(.width(32)) register_3 (.D(WriteData), .en(WEN3), .clk(clk), .Q(x3));  // open: clr
  Register #(.width(32)) register_4 (.D(WriteData), .en(WEN4), .clk(clk), .Q(x4));  // open: clr
  Register #(.width(32)) register_5 (.D(WriteData), .en(WEN5), .clk(clk), .Q(t0));  // open: clr
  Register #(.width(32)) register_6 (.D(WriteData), .en(WEN6), .clk(clk), .Q(t1));  // open: clr
  Register #(.width(32)) register_7 (.D(WriteData), .en(WEN7), .clk(clk), .Q(t2));  // open: clr
  Register #(.width(32)) register_8 (.D(WriteData), .en(WEN24), .clk(clk), .Q(x24));  // open: clr
  Register #(.width(32)) register_9 (.D(WriteData), .en(WEN27), .clk(clk), .Q(x27));  // open: clr
  Register #(.width(32)) register_10 (.D(WriteData), .en(WEN30), .clk(clk), .Q(x30));  // open: clr
  Register #(.width(32)) register_11 (.D(WriteData), .en(WEN8), .clk(clk), .Q(s0));  // open: clr
  Register #(.width(32)) register_12 (.D(WriteData), .en(WEN9), .clk(clk), .Q(s1));  // open: clr
  Register #(.width(32)) register_13 (.D(WriteData), .en(WEN10), .clk(clk), .Q(a0));  // open: clr
  Register #(.width(32)) register_14 (.D(WriteData), .en(WEN11), .clk(clk), .Q(x11));  // open: clr
  Register #(.width(32)) register_15 (.D(WriteData), .en(WEN12), .clk(clk), .Q(x12));  // open: clr
  Register #(.width(32)) register_16 (.D(WriteData), .en(WEN13), .clk(clk), .Q(x13));  // open: clr
  Register #(.width(32)) register_17 (.D(WriteData), .en(WEN14), .clk(clk), .Q(x14));  // open: clr
  Register #(.width(32)) register_18 (.D(WriteData), .en(WEN15), .clk(clk), .Q(x15));  // open: clr
  Register #(.width(32)) register_19 (.D(WriteData), .en(WEN25), .clk(clk), .Q(x25));  // open: clr
  Register #(.width(32)) register_20 (.D(WriteData), .en(WEN28), .clk(clk), .Q(x28));  // open: clr
  Register #(.width(32)) register_21 (.D(WriteData), .en(WEN31), .clk(clk), .Q(x31));  // open: clr
  Register #(.width(32)) register_22 (.D(WriteData), .en(WEN16), .clk(clk), .Q(x16));  // open: clr
  Register #(.width(32)) register_23 (.D(WriteData), .en(WEN17), .clk(clk), .Q(x17));  // open: clr
  Register #(.width(32)) register_24 (.D(WriteData), .en(WEN18), .clk(clk), .Q(x18));  // open: clr
  Register #(.width(32)) register_25 (.D(WriteData), .en(WEN19), .clk(clk), .Q(x19));  // open: clr
  Register #(.width(32)) register_26 (.D(WriteData), .en(WEN20), .clk(clk), .Q(x20));  // open: clr
  Register #(.width(32)) register_27 (.D(WriteData), .en(WEN21), .clk(clk), .Q(x21));  // open: clr
  Register #(.width(32)) register_28 (.D(WriteData), .en(WEN22), .clk(clk), .Q(x22));  // open: clr
  Register #(.width(32)) register_29 (.D(WriteData), .en(WEN26), .clk(clk), .Q(x26));  // open: clr
  Register #(.width(32)) register_30 (.D(WriteData), .en(WEN23), .clk(clk), .Q(x23));  // open: clr
  Register #(.width(32)) register_31 (.D(WriteData), .en(WEN29), .clk(clk), .Q(x29));  // open: clr
  Multiplexer #(.select(5), .width(32)) multiplexer_1 (
    .in0({32{1'b0}}), .in1(ra), .in2(sp), .in3(x3), .in4(x4), .in5(t0), .in6(t1), .in7(t2), .in8(s0),
    .in9(s1), .in10(a0), .in11(x11), .in12(x12), .in13(x13), .in14(x14), .in15(x15), .in16(x16), .in17(x17),
    .in18(x18), .in19(x19), .in20(x20), .in21(x21), .in22(x22), .in23(x23), .in24(x24), .in25(x25),
    .in26(x26), .in27(x27), .in28(x28), .in29(x29), .in30(x30), .in31(x31), .out(ReadData1), .sel(ReadIndex1));
  Multiplexer #(.select(5), .width(32)) multiplexer_2 (
    .in0({32{1'b0}}), .in1(ra), .in2(sp), .in3(x3), .in4(x4), .in5(t0), .in6(t1), .in7(t2), .in8(s0),
    .in9(s1), .in10(a0), .in11(x11), .in12(x12), .in13(x13), .in14(x14), .in15(x15), .in16(x16), .in17(x17),
    .in18(x18), .in19(x19), .in20(x20), .in21(x21), .in22(x22), .in23(x23), .in24(x24), .in25(x25),
    .in26(x26), .in27(x27), .in28(x28), .in29(x29), .in30(x30), .in31(x31), .out(ReadData2), .sel(ReadIndex2));

  // Other names for the same wires on the sheet: x1[31:0] = ra; x2[31:0] = sp; x5[31:0] = t0; x6[31:0] = t1;
  //   x7[31:0] = t2; x8[31:0] = s0; x9[31:0] = s1; x10[31:0] = a0

  // Notes on the sheet:
  //   INPUTS to your circuit
  //   DON'T CHANGE THE LOCATIONS OF THE INPUTS AND OUTPUTS!
  //   These are DEBUG/TEST outputs from your circuit.
  //   OUTPUTS from your circuit
endmodule
